// Logisim project fiscsim.circ as structural Verilog: 1 circuit, main circuit main
module main (
);

  wire and_1_out, and_2_out, clock_1_out, clock_2_out, clock_3_out, decoder_1_out0, decoder_1_out1,
       decoder_1_out2, decoder_1_out3, nor_1_out, not_1_out, not_2_out, register_2_q;
  wire [5:0] adder_1_out, multiplexer_1_out, register_1_q, rom_1_data_2;
  wire [7:0] adder_2_out, and_3_out, multiplexer_2_out, multiplexer_3_out, multiplexer_4_out, not_3_out,
       register_3_q, register_4_q, register_5_q, register_6_q;
  wire [7:6] rom_1_data;

  Multiplexer #(.width(6)) multiplexer_1 (
    .in0(adder_1_out), .in1(rom_1_data_2), .out(multiplexer_1_out), .sel(and_1_out));
  Clock clock_1 (.out(clock_1_out));
  Register #(.width(6)) register_1 (
    .D(multiplexer_1_out), .en(1'b1), .clk(clock_1_out), .Q(register_1_q));  // open: clr
  Adder #(.width(6)) adder_1 (.a(register_1_q), .b(6'b000001), .out(adder_1_out));  // open: cin, cout
  ROM #(.addrWidth(6)) rom_1 (.addr(register_1_q), .data({rom_1_data, rom_1_data_2}));
  not not_1 (not_1_out, register_2_q);
  and and_1 (and_1_out, and_2_out, not_1_out);
  Register #(.width(1)) register_2 (.D(nor_1_out), .en(not_2_out), .clk(clock_2_out), .Q(register_2_q));  // open: clr
  Clock clock_2 (.out(clock_2_out));
  not not_2 (not_2_out, and_2_out);
  and and_2 (and_2_out, rom_1_data[7], rom_1_data[6]);
  Decoder #(.select(2)) decoder_1 (
    .out0(decoder_1_out0), .out1(decoder_1_out1), .out2(decoder_1_out2), .out3(decoder_1_out3),
    .sel(rom_1_data_2[1:0]), .en(not_2_out));
  Register register_3 (.D(multiplexer_4_out), .en(decoder_1_out0), .clk(clock_3_out), .Q(register_3_q));  // open: clr
  Register register_4 (.D(multiplexer_4_out), .en(decoder_1_out1), .clk(clock_3_out), .Q(register_4_q));  // open: clr
  Register register_5 (.D(multiplexer_4_out), .en(decoder_1_out2), .clk(clock_3_out), .Q(register_5_q));  // open: clr
  Register register_6 (.D(multiplexer_4_out), .en(decoder_1_out3), .clk(clock_3_out), .Q(register_6_q));  // open: clr
  Clock clock_3 (.out(clock_3_out));
  Multiplexer #(.select(2), .width(8)) multiplexer_2 (
    .in0(register_3_q), .in1(register_4_q), .in2(register_5_q), .in3(register_6_q), .out(multiplexer_2_out),
    .sel(rom_1_data_2[5:4]));
  nor nor_1 (nor_1_out, multiplexer_4_out[0], multiplexer_4_out[1], multiplexer_4_out[2], multiplexer_4_out[3], multiplexer_4_out[4], multiplexer_4_out[5], multiplexer_4_out[6], multiplexer_4_out[7]);
  Multiplexer #(.select(2), .width(8)) multiplexer_3 (
    .in0(register_3_q), .in1(register_4_q), .in2(register_5_q), .in3(register_6_q), .out(multiplexer_3_out),
    .sel(rom_1_data_2[3:2]));
  Hex_Digit_Display #(.decimalPoint("false")) hex_digit_display_1 (.value(register_6_q[7:4]));
  Adder adder_2 (.a(multiplexer_2_out), .b(multiplexer_3_out), .out(adder_2_out));  // open: cin, cout
  assign and_3_out = multiplexer_2_out & multiplexer_3_out;  // AND_Gate and_3, 8 bits wide
  assign not_3_out = ~multiplexer_2_out;  // NOT_Gate not_3, 8 bits wide
  Hex_Digit_Display #(.decimalPoint("false")) hex_digit_display_2 (.value(register_6_q[3:0]));
  Multiplexer #(.select(2), .width(8)) multiplexer_4 (
    .in0(adder_2_out), .in1(and_3_out), .in2(not_3_out), .in3(not_3_out), .out(multiplexer_4_out),
    .sel(rom_1_data));

  // Notes on the sheet:
  //   contents of rom_1 (hex, n*v repeats v):
  //   90 45 90 2 a2 28 8 0 80 57 6b 56 7d 2f 2e 4 cd 7f d2
endmodule
