// Logisim project CPU_Lab_3.circ as structural Verilog: 6 circuits, main circuit main
module main (
  output [7:0] R0,
  output [7:0] R1,
  output [7:0] R2,
  output [7:0] R3
);

  wire alu_1_cout, alu_1_z, and_1_out, and_2_out, and_3_out, and_4_out, bcd_to_7_segment_decoder_1_p1,
       bcd_to_7_segment_decoder_1_p2, bcd_to_7_segment_decoder_1_p3, bcd_to_7_segment_decoder_1_p4,
       bcd_to_7_segment_decoder_1_p6, bcd_to_7_segment_decoder_1_p7, bcd_to_7_segment_decoder_1_p8,
       bcd_to_7_segment_decoder_2_p1, bcd_to_7_segment_decoder_2_p2, bcd_to_7_segment_decoder_2_p3,
       bcd_to_7_segment_decoder_2_p4, bcd_to_7_segment_decoder_2_p6, bcd_to_7_segment_decoder_2_p7,
       bcd_to_7_segment_decoder_2_p8, bcd_to_7_segment_decoder_3_p1, bcd_to_7_segment_decoder_3_p2,
       bcd_to_7_segment_decoder_3_p3, bcd_to_7_segment_decoder_3_p4, bcd_to_7_segment_decoder_3_p6,
       bcd_to_7_segment_decoder_3_p7, bcd_to_7_segment_decoder_3_p8, bcd_to_7_segment_decoder_4_p1,
       bcd_to_7_segment_decoder_4_p2, bcd_to_7_segment_decoder_4_p3, bcd_to_7_segment_decoder_4_p4,
       bcd_to_7_segment_decoder_4_p6, bcd_to_7_segment_decoder_4_p7, bcd_to_7_segment_decoder_4_p8,
       bcd_to_7_segment_decoder_5_p1, bcd_to_7_segment_decoder_5_p2, bcd_to_7_segment_decoder_5_p3,
       bcd_to_7_segment_decoder_5_p6, bcd_to_7_segment_decoder_5_p7, bcd_to_7_segment_decoder_5_p8,
       bcd_to_7_segment_decoder_6_p1, bcd_to_7_segment_decoder_6_p2, bcd_to_7_segment_decoder_6_p3,
       bcd_to_7_segment_decoder_6_p6, bcd_to_7_segment_decoder_6_p7, bcd_to_7_segment_decoder_6_p8,
       clock_1_out, clock_2_out, clock_3_out, controlcpu_1_regenbl, controlcpu_1_st, decoder_1_out0,
       decoder_1_out1, displaydecoder_1_sign, displaydecoder_2_sign, IOSel_out, not_1_out;
  wire [1:0] controlcpu_1_ld, controlcpu_1_ra0, controlcpu_1_ra1, controlcpu_1_wa0;
  wire [3:0] controlcpu_1_opcodealu, displaydecoder_1_bcd0, displaydecoder_1_bcd1, displaydecoder_1_bcd2,
       displaydecoder_2_bcd0, displaydecoder_2_bcd1, displaydecoder_2_bcd2, regfile4x8_1_rd0_2;
  wire [7:0] alu_1_c, controlcpu_1_im8b, multiplexer_1_out, ram_1_dout, regfile4x8_1_rd1, regfile4x8_1_rd2,
       register_1_q, register_2_q;
  wire [7:4] regfile4x8_1_rd0;
  wire [11:0] rom_1_data;
  wire [12:0] controlcpu_1_addr13b;

  not not_1 (not_1_out, IOSel_out);
  and and_1 (and_1_out, not_1_out, controlcpu_1_ld[0]);
  and and_2 (and_2_out, not_1_out, controlcpu_1_st);
  Clock clock_1 (.out(clock_1_out));
  ROM #(.addrWidth(13), .dataWidth(12)) rom_1 (.addr(controlcpu_1_addr13b), .data(rom_1_data));
  RAM #(.asyncread("true")) ram_1 (
    .addr({regfile4x8_1_rd0, regfile4x8_1_rd0_2}), .we(and_2_out), .oe(and_1_out), .clk(clock_1_out),
    .din(regfile4x8_1_rd2), .dout(ram_1_dout));
  and and_3 (and_3_out, controlcpu_1_st, decoder_1_out0);
  and and_4 (and_4_out, controlcpu_1_st, decoder_1_out1);
  ControlCPU controlcpu_1 (
    .Opcode12b(rom_1_data), .Z(alu_1_z), .COut(alu_1_cout), .RA1(controlcpu_1_ra1), .WA0(controlcpu_1_wa0),
    .RA0(controlcpu_1_ra0), .OpcodeALU(controlcpu_1_opcodealu), .ST(controlcpu_1_st),
    .LD(controlcpu_1_ld[0]), .IM8b(controlcpu_1_im8b), .ADDR13b(controlcpu_1_addr13b),
    .MVI(controlcpu_1_ld[1]), .RegEnbl(controlcpu_1_regenbl));  // open: MOV, BNZ, BCS
  Register register_1 (.D(regfile4x8_1_rd2), .en(and_3_out), .clk(clock_2_out), .Q(register_1_q));  // open: clr
  Clock clock_2 (.out(clock_2_out));
  Register register_2 (.D(regfile4x8_1_rd2), .en(and_4_out), .clk(clock_3_out), .Q(register_2_q));  // open: clr
  Clock clock_3 (.out(clock_3_out));
  Multiplexer #(.select(2), .width(8)) multiplexer_1 (
    .in0(alu_1_c), .in1(ram_1_dout), .in2(controlcpu_1_im8b), .out(multiplexer_1_out), .sel(controlcpu_1_ld));  // open: in3
  DisplayDecoder displaydecoder_1 (
    .BIN8(register_1_q), .BCD2(displaydecoder_1_bcd2), .BCD1(displaydecoder_1_bcd1),
    .BCD0(displaydecoder_1_bcd0), .sign(displaydecoder_1_sign));
  DisplayDecoder displaydecoder_2 (
    .BIN8(register_2_q), .BCD2(displaydecoder_2_bcd2), .BCD1(displaydecoder_2_bcd1),
    .BCD0(displaydecoder_2_bcd0), .sign(displaydecoder_2_sign));
  RegFile4x8 regfile4x8_1 (
    .WD0(multiplexer_1_out), .WA0(controlcpu_1_wa0), .RA0(controlcpu_1_ra0), .Enable(controlcpu_1_regenbl),
    .RA1(controlcpu_1_ra1), .RA2(controlcpu_1_wa0), .RD0({regfile4x8_1_rd0, regfile4x8_1_rd0_2}),
    .RD1(regfile4x8_1_rd1), .RD2(regfile4x8_1_rd2), .R0Dbg(R0), .R1Dbg(R1), .R2Dbg(R2), .R3Dbg(R3));
  ALU alu_1 (
    .a({regfile4x8_1_rd0, regfile4x8_1_rd0_2}), .b(regfile4x8_1_rd1), .opcodeALU(controlcpu_1_opcodealu),
    .z(alu_1_z), .c(alu_1_c), .cout(alu_1_cout));
  // BCD_to_7_Segment_decoder bcd_to_7_segment_decoder_1: pin names not known; wires that end beside it: bcd_to_7_segment_decoder_1_p1, bcd_to_7_segment_decoder_1_p2, bcd_to_7_segment_decoder_1_p3, bcd_to_7_segment_decoder_1_p4, displaydecoder_1_bcd0, bcd_to_7_segment_decoder_1_p6, bcd_to_7_segment_decoder_1_p7, bcd_to_7_segment_decoder_1_p8
  // BCD_to_7_Segment_decoder bcd_to_7_segment_decoder_2: pin names not known; wires that end beside it: bcd_to_7_segment_decoder_2_p1, bcd_to_7_segment_decoder_2_p2, bcd_to_7_segment_decoder_2_p3, bcd_to_7_segment_decoder_2_p4, displaydecoder_2_bcd0, bcd_to_7_segment_decoder_2_p6, bcd_to_7_segment_decoder_2_p7, bcd_to_7_segment_decoder_2_p8
  // BCD_to_7_Segment_decoder bcd_to_7_segment_decoder_3: pin names not known; wires that end beside it: bcd_to_7_segment_decoder_3_p1, bcd_to_7_segment_decoder_3_p2, bcd_to_7_segment_decoder_3_p3, bcd_to_7_segment_decoder_3_p4, displaydecoder_1_bcd1, bcd_to_7_segment_decoder_3_p6, bcd_to_7_segment_decoder_3_p7, bcd_to_7_segment_decoder_3_p8
  // BCD_to_7_Segment_decoder bcd_to_7_segment_decoder_4: pin names not known; wires that end beside it: bcd_to_7_segment_decoder_4_p1, bcd_to_7_segment_decoder_4_p2, bcd_to_7_segment_decoder_4_p3, bcd_to_7_segment_decoder_4_p4, displaydecoder_2_bcd1, bcd_to_7_segment_decoder_4_p6, bcd_to_7_segment_decoder_4_p7, bcd_to_7_segment_decoder_4_p8
  and IOSel (IOSel_out, regfile4x8_1_rd0[4], regfile4x8_1_rd0[5], regfile4x8_1_rd0[6], regfile4x8_1_rd0[7]);
  // BCD_to_7_Segment_decoder bcd_to_7_segment_decoder_5: pin names not known; wires that end beside it: bcd_to_7_segment_decoder_5_p1, bcd_to_7_segment_decoder_5_p2, bcd_to_7_segment_decoder_5_p3, bcd_to_7_segment_decoder_5_p2, displaydecoder_1_bcd2, bcd_to_7_segment_decoder_5_p6, bcd_to_7_segment_decoder_5_p7, bcd_to_7_segment_decoder_5_p8
  // BCD_to_7_Segment_decoder bcd_to_7_segment_decoder_6: pin names not known; wires that end beside it: bcd_to_7_segment_decoder_6_p1, bcd_to_7_segment_decoder_6_p2, bcd_to_7_segment_decoder_6_p3, bcd_to_7_segment_decoder_6_p2, displaydecoder_2_bcd2, bcd_to_7_segment_decoder_6_p6, bcd_to_7_segment_decoder_6_p7, bcd_to_7_segment_decoder_6_p8
  Decoder #(.select(4)) decoder_1 (
    .out0(decoder_1_out0), .out1(decoder_1_out1), .sel(regfile4x8_1_rd0_2), .en(IOSel_out));  // open: out2, out3, out4, out5, out6, out7, out8, out9, out10, out11, out12, out13, out14, out15
  _7_Segment_Display u_7_segment_display_1 (.g(displaydecoder_1_sign));  // open: f, a, b, e, d, c, dp
  _7_Segment_Display u_7_segment_display_2 (
    .g(bcd_to_7_segment_decoder_5_p1), .f(bcd_to_7_segment_decoder_5_p3), .a(bcd_to_7_segment_decoder_5_p6),
    .b(bcd_to_7_segment_decoder_5_p8), .e(bcd_to_7_segment_decoder_5_p2), .d(bcd_to_7_segment_decoder_5_p2),
    .c(bcd_to_7_segment_decoder_5_p7));  // open: dp
  _7_Segment_Display u_7_segment_display_3 (.g(displaydecoder_2_sign));  // open: f, a, b, e, d, c, dp
  _7_Segment_Display u_7_segment_display_4 (
    .g(bcd_to_7_segment_decoder_6_p1), .f(bcd_to_7_segment_decoder_6_p3), .a(bcd_to_7_segment_decoder_6_p6),
    .b(bcd_to_7_segment_decoder_6_p8), .e(bcd_to_7_segment_decoder_6_p2), .d(bcd_to_7_segment_decoder_6_p2),
    .c(bcd_to_7_segment_decoder_6_p7));  // open: dp
  _7_Segment_Display u_7_segment_display_5 (
    .g(bcd_to_7_segment_decoder_3_p1), .f(bcd_to_7_segment_decoder_3_p3), .a(bcd_to_7_segment_decoder_3_p6),
    .b(bcd_to_7_segment_decoder_3_p8), .e(bcd_to_7_segment_decoder_3_p2), .d(bcd_to_7_segment_decoder_3_p4),
    .c(bcd_to_7_segment_decoder_3_p7));  // open: dp
  _7_Segment_Display u_7_segment_display_6 (
    .g(bcd_to_7_segment_decoder_1_p1), .f(bcd_to_7_segment_decoder_1_p3), .a(bcd_to_7_segment_decoder_1_p6),
    .b(bcd_to_7_segment_decoder_1_p8), .e(bcd_to_7_segment_decoder_1_p2), .d(bcd_to_7_segment_decoder_1_p4),
    .c(bcd_to_7_segment_decoder_1_p7), .dp(bcd_to_7_segment_decoder_1_p7));
  _7_Segment_Display u_7_segment_display_7 (
    .g(bcd_to_7_segment_decoder_4_p1), .f(bcd_to_7_segment_decoder_4_p3), .a(bcd_to_7_segment_decoder_4_p6),
    .b(bcd_to_7_segment_decoder_4_p8), .e(bcd_to_7_segment_decoder_4_p2), .d(bcd_to_7_segment_decoder_4_p4),
    .c(bcd_to_7_segment_decoder_4_p7));  // open: dp
  _7_Segment_Display u_7_segment_display_8 (
    .g(bcd_to_7_segment_decoder_2_p1), .f(bcd_to_7_segment_decoder_2_p3), .a(bcd_to_7_segment_decoder_2_p6),
    .b(bcd_to_7_segment_decoder_2_p8), .e(bcd_to_7_segment_decoder_2_p2), .d(bcd_to_7_segment_decoder_2_p4),
    .c(bcd_to_7_segment_decoder_2_p7), .dp(bcd_to_7_segment_decoder_2_p7));

  // Notes on the sheet:
  //   contents of rom_1 (hex, n*v repeats v):
  //   c01 c06 fb8 310 19 fbc 310 19 fbc 310 19 fbc 310 19 fc0 310 19 fc0 310 19 fc4 310 19 fc8 310 19 fc8
  //   310 19 fcc 310 19 fc8 310 19 fd0 310 19 fd0 310 19 fd4 310 19 fd4 310 19 fd8 310 19 fdc 310 19 fdc
  //   310 19 fe0 310 19 fe0 310 19 fe4 310 19 fe4 310 19 fe8 310 19 fe8 310 19 fec 310 19 ff0 310 19 ff0
  //   310 19 ff4 310 19 ff4 310 19 fd8 310 19 fd8 310 19 ffc 310 19 ffc 310 19 c00 310 19 c04 310 19 c04
  //   310 19 c08 310 19 c08 310 19 c0c 310 19 c0c 310 19 c10 310 19 c10 310 19 c14 310 19 c18 310 19 c18
  //   310 19 c1c 310 19 c1c 310 19 c20 310 19 c20 310 19 c24 310 19 c24 310 19 c28 310 19 c2c 310 19 c2c
  //   310 19 c30 310 19 c30 310 19 c34 310 19 c34 310 19 c38 310 19 c38 310 19 c3c 310 19 c40 310 19 c40
  //   310 19 c44 310 19 c44 310 19 c48 310 19 c48 310 19 c4c 310 19 c4c 310 19 c50 310 19 c54 310 19 c54
  //   310 19 c58 310 19 c58 310 19 c5c 310 19 c5c 310 19 c60 310 19 c60 310 19 c64 310 19 c68 310 19 c68
  //   310 19 c6c 310 19 c6c 310 19 c70 310 19 c70 310 19 c74 310 19 c74 310 19 c78 310 19 c7c 310 19 c7c
  //   310 19 c80 310 19 c80 310 19 c84 310 19 c84 310 19 c88 310 19 c88 310 19 c8c 310 19 c90 310 19 c90
  //   310 19 c94 310 19 c94 310 19 c98 310 19 c98 310 19 c9c 310 19 c9c 310 19 ca0 310 19 ca4 310 19 ca4
  //   310 19 ca8 310 19 ca8 310 19 cac 310 19 cac 310 19 cb0 310 19 cb0 310 19 cb4 310 19 cb8 310 19 cb8
  //   310 19 cbc 310 19 cbc 310 19 cc0 310 19 cc0 310 19 cc4 310 19 cc4 310 19 cc8 310 19 ccc 310 19 ccc
  //   310 19 cd0 310 19 cd0 310 19 cd4 310 19 e9c 310 19 ea0 310 19 ea0 310 19 ea4 310 19 ea4 310 19 ea8
  //   310 19 ea8 310 19 eac 310 19 eb0 310 19 eb0 310 19 eb4 310 19 eb4 310 19 eb8 310 19 eb8 310 19 ebc
  //   310 19 ebc 310 19 ec0 310 19 ec4 310 19 ec4 310 19 ec8 310 19 ec8 310 19 ecc 310 19 ecc 310 19 ed0
  //   310 19 ed0 310 19 ed4 310 19 ed8 310 19 ed8 310 19 edc 310 19 edc 310 19 ee0 310 19 ee0 310 19 ee4
  //   310 19 ee4 310 19 ee8 310 19 eec 310 19 eec 310 19 ef0 310 19 ef0 310 19 ef0 310 19 ef4 310 19 ef8
  //   310 19 ef8 310 19 efc 310 19 f00 310 19 f00 310 19 f04 310 19 f04 310 19 f08 310 19 f08 310 19 f0c
  //   310 19 f0c 310 19 f10 310 19 f10 310 19 f14 310 19 f18 310 19 f18 310 19 f1c 310 19 f1c 310 19 f20
  //   310 19 f20 310 19 f24 310 19 f28 310 19 f28 310 19 f2c 310 19 f2c 310 19 f30 310 19 f30 310 19 f34
  //   310 19 f34 310 19 f38 310 19 f3c 310 19 f3c 310 19 f40 310 19 f44 310 19 f44 310 19 f48 310 19 f48
  //   310 19 f4c 310 19 f50 310 19 f50 310 19 f54 310 19 f54 310 19 f58 310 19 f58 310 19 f5c 310 19 f5c
  //   310 19 f60 310 19 f64 310 19 f64 310 19 f68 310 19 f68 310 19 f6c 310 19 f6c 310 19 f70 310 19 f70
  //   310 19 f74 310 19 f78 310 19 f78 310 19 f7c 310 19 f7c 310 19 f80 310 19 f80 310 19 f84 310 19 f84
  //   310 19 f88 310 19 f8c 310 19 f8c 310 19 f90 310 19 f90 310 19 f94 310 19 f94 310 19 f98 310 19 f98
  //   310 19 f9c 310 19 fa0 310 19 fa0 310 19 fa4 310 19 fa4 310 19 fa8 310 19 fa8 310 19 fac 310 19 fac
  //   310 19 fb0 310 19 fb4 310 19 fb4 310 19 fb8 310 19 c04 c02 363 fc1 312 11 313 22 7fa
  //   Debug Registers
  //   Fahrenheit
  //   Celsius
endmodule

module FourBitCLA (
  input  cin,
  input  [3:0] a03,
  input  [3:0] b03,
  output [3:0] s03,
  output cout
);

  wire and_1_out, and_2_out, and_3_out, and_4_out, nand_1_out, nand_2_out, nand_3_out, nand_4_out,
       nand_5_out, nand_6_out, nand_7_out, nand_8_out, nand_9_out, nand_10_out, nand_11_out, nand_12_out,
       nand_13_out, not_1_out, not_2_out, not_3_out, not_4_out, xor_1_out, xor_2_out, xor_3_out, xor_4_out;

  and and_1 (and_1_out, a03[0], b03[0]);
  xor xor_1 (xor_1_out, a03[0], b03[0]);
  and and_2 (and_2_out, a03[1], b03[1]);
  xor xor_2 (xor_2_out, a03[1], b03[1]);
  and and_3 (and_3_out, a03[2], b03[2]);
  xor xor_3 (xor_3_out, a03[2], b03[2]);
  and and_4 (and_4_out, a03[3], b03[3]);
  xor xor_4 (xor_4_out, a03[3], b03[3]);
  xor xor_5 (s03[0], xor_1_out, cin);
  xor xor_6 (s03[1], xor_2_out, nand_11_out);
  xor xor_7 (s03[2], xor_3_out, nand_12_out);
  xor xor_8 (s03[3], xor_4_out, nand_13_out);
  not not_1 (not_1_out, and_1_out);
  not not_2 (not_2_out, and_2_out);
  nand nand_1 (nand_1_out, and_1_out, xor_2_out);
  nand nand_2 (nand_2_out, cin, xor_1_out, xor_2_out);
  not not_3 (not_3_out, and_3_out);
  nand nand_3 (nand_3_out, and_2_out, xor_3_out);
  nand nand_4 (nand_4_out, and_1_out, xor_2_out, xor_3_out);
  nand nand_5 (nand_5_out, cin, xor_1_out, xor_2_out, xor_3_out);
  nand nand_6 (nand_6_out, xor_4_out, and_3_out);
  nand nand_7 (nand_7_out, xor_4_out, xor_3_out, and_2_out);
  nand nand_8 (nand_8_out, xor_4_out, xor_3_out, xor_2_out, and_1_out);
  nand nand_9 (nand_9_out, xor_4_out, xor_3_out, xor_2_out, xor_1_out, cin);
  nand nand_10 (nand_10_out, xor_1_out, cin);
  not not_4 (not_4_out, and_4_out);
  nand nand_11 (nand_11_out, not_1_out, nand_10_out);
  nand nand_12 (nand_12_out, not_2_out, nand_1_out, nand_2_out);
  nand nand_13 (nand_13_out, not_3_out, nand_3_out, nand_4_out, nand_5_out);
  nand nand_14 (cout, not_4_out, nand_6_out, nand_7_out, nand_8_out, nand_9_out);
endmodule

module ALU (
  input  [7:0] a,
  input  [7:0] b,
  input  [3:0] opcodeALU,
  output z,
  output [7:0] c,
  output cout
);

  wire and_1_out, and_3_out, and_4_out, and_6_out, and_7_out, and_8_out, and_9_out, and_10_out, and_11_out,
       and_12_out, and_13_out, and_14_out, and_15_out, and_16_out, decoder_1_out1, decoder_1_out5,
       fourbitcla_1_cout, not_2_out;
  wire [7:0] and_2_out, and_5_out, fourbitcla_2_s03, multiplexer_1_out, not_1_out, not_3_out, or_2_out;

  assign not_1_out = ~b;  // NOT_Gate not_1, 8 bits wide
  Decoder #(.select(4)) decoder_1 (
    .out1(decoder_1_out1), .out5(decoder_1_out5), .sel(opcodeALU));  // open: out0, out2, out3, out4, out6, out7, out8, out9, out10, out11, out12, out13, out14, out15, en
  not not_2 (not_2_out, decoder_1_out5);
  Multiplexer #(.width(8)) multiplexer_1 (.in0(b), .in1(not_1_out), .out(multiplexer_1_out), .sel(decoder_1_out1));
  and and_1 (and_1_out, a[0], decoder_1_out5);
  and and_2 (and_2_out[0], not_2_out, a[1]);
  or or_1 (and_2_out[1], and_1_out, and_4_out);
  assign not_3_out = ~a;  // NOT_Gate not_3, 8 bits wide
  and and_3 (and_3_out, a[1], decoder_1_out5);
  and and_4 (and_4_out, not_2_out, a[2]);
  assign and_5_out = a & multiplexer_1_out;  // AND_Gate and_5, 8 bits wide
  assign or_2_out = a | multiplexer_1_out;  // OR_Gate or_2, 8 bits wide
  and and_6 (and_6_out, a[2], decoder_1_out5);
  or or_3 (and_2_out[2], and_3_out, and_7_out);
  and and_7 (and_7_out, not_2_out, a[3]);
  and and_8 (and_8_out, a[3], decoder_1_out5);
  or or_4 (and_2_out[3], and_6_out, and_9_out);
  and and_9 (and_9_out, not_2_out, a[4]);
  FourBitCLA fourbitcla_1 (
    .cin(decoder_1_out1), .a03(a[3:0]), .b03(multiplexer_1_out[3:0]), .s03(fourbitcla_2_s03[3:0]),
    .cout(fourbitcla_1_cout));
  FourBitCLA fourbitcla_2 (
    .cin(fourbitcla_1_cout), .a03(a[7:4]), .b03(multiplexer_1_out[7:4]), .s03(fourbitcla_2_s03[7:4]),
    .cout(cout));
  and and_10 (and_10_out, a[4], decoder_1_out5);
  or or_5 (and_2_out[4], and_8_out, and_11_out);
  and and_11 (and_11_out, not_2_out, a[5]);
  or or_6 (and_2_out[5], and_10_out, and_13_out);
  and and_12 (and_12_out, a[5], decoder_1_out5);
  and and_13 (and_13_out, not_2_out, a[6]);
  and and_14 (and_14_out, a[6], decoder_1_out5);
  or or_7 (and_2_out[6], and_12_out, and_15_out);
  Multiplexer #(.select(4), .width(8)) multiplexer_2 (
    .in0(fourbitcla_2_s03), .in1(fourbitcla_2_s03), .in2(and_5_out), .in3(or_2_out), .in4(not_3_out),
    .in5(and_2_out), .in6(and_2_out), .in8(a), .out(c), .sel(opcodeALU));  // open: in7, in9, in10, in11, in12, in13, in14, in15
  and and_15 (and_15_out, not_2_out, a[7]);
  and and_16 (and_16_out, not_2_out, a[7]);
  or or_8 (and_2_out[7], and_14_out, and_16_out);
  nor nor_1 (z, c[0], c[1], c[2], c[3], c[4], c[5], c[6], c[7]);
endmodule

module RegFile4x8 (
  input  [7:0] WD0,
  input  [1:0] WA0,
  input  [1:0] RA0,
  input  Enable,
  input  [1:0] RA1,
  input  [1:0] RA2,
  output [7:0] RD0,
  output [7:0] RD1,
  output [7:0] RD2,
  output [7:0] R0Dbg,
  output [7:0] R1Dbg,
  output [7:0] R2Dbg,
  output [7:0] R3Dbg
);

  wire clock_1_out, decoder_1_out0, decoder_1_out1, decoder_1_out2, decoder_1_out3;

  Decoder #(.select(2)) decoder_1 (
    .out0(decoder_1_out0), .out1(decoder_1_out1), .out2(decoder_1_out2), .out3(decoder_1_out3), .sel(WA0),
    .en(Enable));
  Clock clock_1 (.out(clock_1_out));
  Register register_1 (.D(WD0), .en(decoder_1_out0), .clk(clock_1_out), .Q(R0Dbg));  // open: clr
  Register register_2 (.D(WD0), .en(decoder_1_out1), .clk(clock_1_out), .Q(R1Dbg));  // open: clr
  Register register_3 (.D(WD0), .en(decoder_1_out2), .clk(clock_1_out), .Q(R2Dbg));  // open: clr
  Register register_4 (.D(WD0), .en(decoder_1_out3), .clk(clock_1_out), .Q(R3Dbg));  // open: clr
  Multiplexer #(.select(2), .width(8)) multiplexer_1 (
    .in0(R0Dbg), .in1(R1Dbg), .in2(R2Dbg), .in3(R3Dbg), .out(RD0), .sel(RA0));
  Multiplexer #(.select(2), .width(8)) multiplexer_2 (
    .in0(R0Dbg), .in1(R1Dbg), .in2(R2Dbg), .in3(R3Dbg), .out(RD1), .sel(RA1));
  Multiplexer #(.select(2), .width(8)) multiplexer_3 (
    .in0(R0Dbg), .in1(R1Dbg), .in2(R2Dbg), .in3(R3Dbg), .out(RD2), .sel(RA2));
endmodule

module DisplayDecoder (
  input  [7:0] BIN8,
  output [3:0] BCD2,
  output [3:0] BCD1,
  output [3:0] BCD0,
  output sign
);

  wire and_6_out, and_7_out, and_8_out, and_9_out, and_10_out, and_11_out, not_1_out, not_2_out, not_3_out,
       not_4_out, not_5_out, not_6_out, not_7_out, not_8_out, or_1_out, or_2_out, or_3_out, or_4_out,
       or_5_out, or_6_out, or_7_out, or_8_out, or_9_out, or_10_out, or_11_out, or_12_out, or_13_out,
       or_14_out, or_15_out, or_16_out, or_17_out, or_18_out, or_19_out, or_20_out, or_21_out, or_22_out,
       or_23_out, or_24_out, or_25_out, or_26_out, or_27_out, or_28_out, or_29_out, or_30_out, or_31_out,
       or_32_out, or_33_out, or_34_out, or_35_out, or_36_out, or_37_out, or_38_out, or_39_out, or_40_out,
       or_41_out, or_42_out, or_43_out, or_44_out, or_45_out, or_46_out, or_47_out, or_48_out, or_49_out,
       or_50_out, or_51_out, or_52_out, or_53_out, or_54_out, or_55_out, or_56_out, or_57_out, or_58_out,
       or_59_out, or_60_out, or_61_out, or_62_out, or_63_out, or_64_out, or_65_out, or_66_out, or_67_out,
       or_68_out, or_69_out, or_70_out, or_71_out, or_72_out, or_73_out, or_74_out, or_75_out, or_76_out,
       or_77_out, or_78_out, or_79_out, or_80_out, or_81_out, or_82_out, or_83_out, or_84_out, or_85_out,
       or_86_out, or_87_out, or_88_out, or_89_out, or_90_out, or_91_out, or_92_out, or_93_out, or_94_out,
       or_95_out, or_96_out, or_97_out, or_98_out, or_99_out, or_100_out, or_101_out, or_102_out, or_103_out,
       or_104_out, or_105_out, or_106_out, or_107_out, or_108_out, or_109_out, or_110_out, or_111_out,
       or_112_out, or_113_out, or_114_out, or_115_out, or_116_out, or_117_out, or_118_out, or_119_out,
       or_120_out, or_121_out, or_122_out, or_123_out, or_124_out, or_125_out, or_126_out, or_127_out,
       or_128_out, or_129_out, or_130_out, or_131_out, or_132_out, or_133_out, or_134_out, or_135_out,
       or_136_out, or_137_out, or_138_out, or_139_out, or_140_out, or_141_out, or_142_out, or_143_out,
       or_144_out, or_145_out, or_146_out, or_147_out, or_148_out, or_149_out, or_150_out, or_151_out,
       or_152_out, or_153_out, or_154_out, or_155_out, or_156_out, or_157_out, or_158_out, or_159_out,
       or_160_out, or_161_out, or_162_out, or_163_out, or_164_out, or_165_out, or_166_out, or_167_out,
       or_168_out, or_169_out, or_170_out, or_171_out, or_172_out, or_173_out, or_174_out, or_175_out,
       or_176_out, or_177_out, or_178_out, or_179_out, or_180_out, or_181_out, or_182_out, or_183_out,
       or_184_out, or_185_out, or_186_out, or_187_out, or_188_out, or_189_out, or_190_out, or_191_out,
       or_192_out, or_193_out, or_194_out, or_195_out, or_196_out, or_197_out, or_198_out, or_199_out,
       or_200_out, or_201_out, or_202_out, or_203_out, or_204_out, or_205_out, or_206_out, or_207_out,
       or_208_out, or_209_out, or_210_out, or_211_out, or_212_out, or_213_out, or_214_out, or_215_out,
       or_216_out, or_217_out, or_218_out, or_219_out, or_220_out, or_221_out, or_222_out, or_223_out,
       or_224_out, or_225_out, or_226_out, or_227_out, or_228_out, or_229_out, or_230_out, or_231_out,
       or_232_out, or_233_out, or_234_out, or_235_out, or_236_out, or_237_out, or_238_out, or_239_out,
       or_240_out, or_241_out, or_242_out, or_243_out, or_244_out, or_245_out, or_246_out, or_247_out,
       or_248_out, or_249_out, or_250_out, or_251_out, or_252_out, or_253_out, or_254_out, or_255_out,
       or_256_out, or_257_out, or_258_out, or_259_out, or_260_out, or_261_out, or_262_out, or_263_out,
       or_264_out, or_265_out, or_266_out, or_267_out, or_268_out, or_269_out, or_270_out, or_271_out,
       or_272_out, or_273_out, or_274_out, or_275_out, or_276_out, or_277_out, or_278_out, or_279_out,
       or_280_out, or_281_out, or_282_out, or_283_out, or_284_out, or_285_out, or_286_out, or_287_out,
       or_288_out, or_289_out, or_290_out, or_291_out, or_292_out, or_293_out, or_294_out, or_295_out,
       or_296_out, or_297_out, or_298_out, or_299_out, or_300_out, or_301_out, or_302_out, or_303_out,
       or_304_out, or_305_out, or_306_out, or_307_out, or_308_out, or_309_out, or_310_out, or_311_out,
       or_312_out, or_313_out, or_314_out, or_315_out, or_316_out, or_317_out, or_318_out, or_319_out,
       or_320_out, or_321_out, or_322_out, or_323_out, or_324_out, or_325_out, or_326_out, or_327_out,
       or_328_out, or_329_out, or_330_out, or_331_out, or_332_out, or_333_out, or_334_out, or_335_out,
       or_336_out, or_337_out, or_338_out, or_339_out, or_340_out, or_341_out, or_342_out, or_343_out,
       or_344_out, or_345_out, or_346_out, or_347_out, or_348_out, or_349_out, or_350_out, or_351_out,
       or_352_out, or_353_out, or_354_out, or_355_out, or_356_out, or_357_out;

  not not_1 (not_1_out, BIN8[7]);
  not not_2 (not_2_out, BIN8[6]);
  not not_3 (not_3_out, BIN8[5]);
  not not_4 (not_4_out, BIN8[4]);
  not not_5 (not_5_out, BIN8[3]);
  not not_6 (not_6_out, BIN8[2]);
  not not_7 (not_7_out, BIN8[1]);
  not not_8 (not_8_out, BIN8[0]);
  or or_1 (or_1_out, BIN8[7], BIN8[5]);
  or or_2 (or_2_out, BIN8[7], BIN8[4], BIN8[3], BIN8[2]);
  or or_3 (or_3_out, BIN8[7], BIN8[6]);
  or or_4 (or_4_out, BIN8[5], not_4_out, not_5_out, not_6_out, not_8_out);
  or or_5 (or_5_out, BIN8[5], not_4_out, not_5_out, not_6_out, not_7_out);
  or or_6 (or_6_out, not_3_out, BIN8[4], BIN8[3], BIN8[2]);
  or or_7 (or_7_out, BIN8[6], not_3_out);
  or or_8 (or_8_out, not_2_out, BIN8[5]);
  or or_9 (or_9_out, not_1_out, not_2_out);
  or or_10 (or_10_out, BIN8[7], BIN8[6]);
  or or_11 (or_11_out, BIN8[5], BIN8[4]);
  or or_12 (or_12_out, not_1_out, not_2_out);
  or or_13 (or_13_out, BIN8[7], not_3_out, not_6_out);
  or or_14 (or_14_out, BIN8[7], not_3_out, not_5_out);
  or or_15 (or_15_out, not_2_out, not_3_out, not_4_out);
  or or_16 (or_16_out, BIN8[6], BIN8[5], BIN8[3]);
  or or_17 (or_17_out, BIN8[6], BIN8[5], BIN8[2]);
  or or_18 (or_18_out, BIN8[6], BIN8[5], BIN8[1], BIN8[0]);
  or or_19 (or_19_out, BIN8[6], not_4_out, BIN8[3], not_8_out);
  or or_20 (or_20_out, BIN8[6], not_4_out, BIN8[3], not_7_out);
  or or_21 (or_21_out, BIN8[6], not_4_out, BIN8[3], not_6_out);
  or or_22 (or_22_out, BIN8[6], not_4_out, not_5_out, BIN8[2]);
  or or_23 (or_23_out, BIN8[6], not_4_out, not_6_out, BIN8[1], BIN8[0]);
  or or_24 (or_24_out, not_3_out, not_4_out, not_5_out);
  or or_25 (or_25_out, BIN8[6], BIN8[5]);
  or or_26 (or_26_out, not_2_out, not_3_out);
  or or_27 (or_27_out, BIN8[6], BIN8[4], BIN8[3]);
  or or_28 (or_28_out, BIN8[7], BIN8[5], not_4_out);
  or or_29 (or_29_out, not_1_out, BIN8[6], BIN8[4]);
  or or_30 (or_30_out, not_1_out, BIN8[6], BIN8[3], BIN8[2], BIN8[1], BIN8[0]);
  or or_31 (or_31_out, BIN8[5], not_4_out, not_5_out, not_8_out);
  or or_32 (or_32_out, BIN8[5], not_4_out, not_5_out, not_7_out);
  or or_33 (or_33_out, BIN8[5], not_4_out, not_5_out, not_6_out);
  or or_34 (or_34_out, BIN8[7], BIN8[6], BIN8[5], BIN8[4]);
  or or_35 (or_35_out, BIN8[7], not_3_out, not_4_out, BIN8[3]);
  or or_36 (or_36_out, BIN8[7], not_2_out, BIN8[5], not_4_out);
  or or_37 (or_37_out, not_1_out, BIN8[6], not_3_out, BIN8[4]);
  or or_38 (or_38_out, not_1_out, not_2_out, not_3_out, not_4_out);
  or or_39 (or_39_out, BIN8[5], not_4_out, BIN8[3], BIN8[2]);
  or or_40 (or_40_out, BIN8[7], BIN8[6], not_3_out, not_5_out, BIN8[2]);
  or or_41 (or_41_out, BIN8[7], not_2_out, not_3_out, BIN8[4]);
  or or_42 (or_42_out, not_4_out, BIN8[3], BIN8[2], BIN8[1], BIN8[0]);
  or or_43 (or_43_out, not_1_out, BIN8[5], not_4_out, BIN8[3]);
  or or_44 (or_44_out, BIN8[6], BIN8[4], not_5_out, not_6_out);
  or or_45 (or_45_out, not_1_out, not_2_out, BIN8[5], BIN8[4], not_6_out, not_8_out);
  or or_46 (or_46_out, not_1_out, not_2_out, BIN8[5], BIN8[4], not_6_out, not_7_out);
  or or_47 (or_47_out, not_1_out, BIN8[6], BIN8[5], not_4_out);
  or or_48 (or_48_out, not_1_out, not_2_out, BIN8[5], BIN8[4], not_5_out);
  or or_49 (or_49_out, not_1_out, BIN8[5], BIN8[4], not_5_out, not_8_out);
  or or_50 (or_50_out, not_1_out, BIN8[5], BIN8[4], not_5_out, not_7_out);
  or or_51 (or_51_out, not_1_out, not_2_out, BIN8[5], not_5_out, BIN8[2], BIN8[1], BIN8[0]);
  or or_52 (or_52_out, not_3_out, BIN8[4], not_5_out, not_6_out, not_8_out);
  or or_53 (or_53_out, not_3_out, BIN8[4], not_5_out, not_6_out, not_7_out);
  or or_54 (or_54_out, BIN8[6], BIN8[5], not_4_out, not_5_out, BIN8[2]);
  or or_55 (or_55_out, BIN8[7], BIN8[6], not_3_out, not_4_out, BIN8[3], BIN8[2], BIN8[1]);
  or or_56 (or_56_out, not_2_out, not_3_out, BIN8[4], BIN8[3], not_6_out);
  or or_57 (or_57_out, BIN8[6], not_3_out, not_4_out, BIN8[3], BIN8[2], BIN8[1], BIN8[0]);
  or or_58 (or_58_out, not_1_out, not_2_out, BIN8[5], BIN8[4], not_5_out, not_6_out, not_7_out, not_8_out);
  or or_59 (or_59_out, BIN8[6], BIN8[5], BIN8[4], BIN8[3]);
  or or_60 (or_60_out, BIN8[6], BIN8[5], BIN8[4], BIN8[2], BIN8[1], BIN8[0]);
  or or_61 (or_61_out, BIN8[7], BIN8[6], BIN8[5], BIN8[4], BIN8[2], BIN8[1]);
  or or_62 (or_62_out, BIN8[6], BIN8[5], BIN8[3], not_6_out);
  or or_63 (or_63_out, BIN8[6], BIN8[5], not_4_out, not_6_out, BIN8[1], BIN8[0]);
  or or_64 (or_64_out, BIN8[7], BIN8[6], BIN8[5], not_4_out, not_6_out, BIN8[1]);
  or or_65 (or_65_out, BIN8[6], BIN8[4], not_5_out, BIN8[2], BIN8[1], BIN8[0]);
  or or_66 (or_66_out, BIN8[7], BIN8[6], BIN8[4], not_5_out, BIN8[2], BIN8[1]);
  or or_67 (or_67_out, BIN8[6], not_3_out, BIN8[4], not_5_out);
  or or_68 (or_68_out, BIN8[6], not_4_out, not_5_out, not_6_out, BIN8[1], BIN8[0]);
  or or_69 (or_69_out, BIN8[7], BIN8[6], not_4_out, not_5_out, not_6_out, BIN8[1]);
  or or_70 (or_70_out, BIN8[6], not_3_out, not_5_out, not_6_out);
  or or_71 (or_71_out, BIN8[5], BIN8[4], BIN8[3], BIN8[2]);
  or or_72 (or_72_out, BIN8[5], BIN8[4], BIN8[3], BIN8[1], BIN8[0]);
  or or_73 (or_73_out, BIN8[7], BIN8[5], BIN8[4], BIN8[3], BIN8[1]);
  or or_74 (or_74_out, not_2_out, BIN8[5], BIN8[3], BIN8[2]);
  or or_75 (or_75_out, not_2_out, BIN8[5], BIN8[3], BIN8[1], BIN8[0]);
  or or_76 (or_76_out, BIN8[7], not_2_out, BIN8[5], BIN8[3], BIN8[1]);
  or or_77 (or_77_out, not_2_out, BIN8[5], not_4_out, BIN8[3]);
  or or_78 (or_78_out, not_2_out, BIN8[5], not_4_out, BIN8[2], BIN8[1], BIN8[0]);
  or or_79 (or_79_out, BIN8[7], not_2_out, BIN8[5], not_4_out, BIN8[2], BIN8[1]);
  or or_80 (or_80_out, not_3_out, BIN8[4], not_5_out, BIN8[2]);
  or or_81 (or_81_out, not_3_out, BIN8[4], not_5_out, BIN8[1], BIN8[0]);
  or or_82 (or_82_out, BIN8[7], not_3_out, BIN8[4], not_5_out, BIN8[1]);
  or or_83 (or_83_out, not_2_out, not_4_out, not_5_out, BIN8[2], BIN8[1], BIN8[0]);
  or or_84 (or_84_out, BIN8[7], not_2_out, not_4_out, not_5_out, BIN8[2], BIN8[1]);
  or or_85 (or_85_out, not_2_out, not_3_out, not_5_out, BIN8[2]);
  or or_86 (or_86_out, not_3_out, not_5_out, not_6_out, BIN8[1], BIN8[0]);
  or or_87 (or_87_out, BIN8[7], not_3_out, not_5_out, not_6_out, BIN8[1]);
  or or_88 (or_88_out, not_2_out, not_3_out, not_4_out, not_5_out);
  or or_89 (or_89_out, not_1_out, BIN8[6], BIN8[5], BIN8[3], not_7_out, not_8_out);
  or or_90 (or_90_out, not_1_out, BIN8[6], BIN8[4], BIN8[3], not_6_out, not_7_out, not_8_out);
  or or_91 (or_91_out, not_1_out, BIN8[6], not_3_out, not_5_out, not_7_out, not_8_out);
  or or_92 (or_92_out, not_1_out, not_2_out, BIN8[4], BIN8[3], BIN8[2], not_7_out, not_8_out);
  or or_93 (or_93_out, not_1_out, not_2_out, not_4_out, BIN8[3], not_6_out, not_7_out, not_8_out);
  or or_94 (or_94_out, not_1_out, BIN8[5], not_5_out, BIN8[1], BIN8[0]);
  or or_95 (or_95_out, BIN8[7], BIN8[6], BIN8[5], BIN8[4], BIN8[3]);
  or or_96 (or_96_out, BIN8[7], BIN8[6], BIN8[5], BIN8[4], not_7_out);
  or or_97 (or_97_out, BIN8[6], BIN8[5], BIN8[4], not_6_out);
  or or_98 (or_98_out, BIN8[7], BIN8[6], BIN8[5], BIN8[3], BIN8[1]);
  or or_99 (or_99_out, BIN8[7], BIN8[6], BIN8[5], BIN8[3], not_6_out);
  or or_100 (or_100_out, BIN8[6], BIN8[5], not_4_out, BIN8[2], BIN8[1]);
  or or_101 (or_101_out, BIN8[7], BIN8[6], BIN8[5], not_5_out, not_7_out);
  or or_102 (or_102_out, BIN8[7], BIN8[6], BIN8[4], BIN8[3], BIN8[2]);
  or or_103 (or_103_out, BIN8[7], BIN8[6], BIN8[4], BIN8[3], BIN8[1]);
  or or_104 (or_104_out, BIN8[7], BIN8[6], not_3_out, BIN8[4], BIN8[2]);
  or or_105 (or_105_out, BIN8[7], BIN8[6], not_3_out, BIN8[4], BIN8[1]);
  or or_106 (or_106_out, BIN8[7], BIN8[6], BIN8[4], not_5_out, not_7_out);
  or or_107 (or_107_out, BIN8[7], BIN8[6], not_3_out, BIN8[3], BIN8[2], not_7_out);
  or or_108 (or_108_out, BIN8[7], BIN8[6], BIN8[3], not_6_out, BIN8[1]);
  or or_109 (or_109_out, BIN8[7], BIN8[6], not_3_out, not_4_out, BIN8[3], not_7_out);
  or or_110 (or_110_out, BIN8[7], BIN8[6], not_3_out, not_5_out, BIN8[1]);
  or or_111 (or_111_out, BIN8[7], BIN8[6], not_5_out, not_6_out, not_7_out);
  or or_112 (or_112_out, BIN8[7], BIN8[5], BIN8[4], BIN8[3], BIN8[2]);
  or or_113 (or_113_out, BIN8[7], BIN8[5], BIN8[4], BIN8[3], not_7_out);
  or or_114 (or_114_out, not_2_out, BIN8[5], BIN8[4], BIN8[2]);
  or or_115 (or_115_out, BIN8[5], BIN8[4], not_5_out, not_6_out, BIN8[1]);
  or or_116 (or_116_out, BIN8[7], BIN8[5], BIN8[3], BIN8[2], BIN8[1]);
  or or_117 (or_117_out, BIN8[7], not_2_out, BIN8[5], BIN8[3], BIN8[2]);
  or or_118 (or_118_out, BIN8[7], BIN8[5], not_4_out, BIN8[3], BIN8[1]);
  or or_119 (or_119_out, BIN8[7], BIN8[5], BIN8[3], not_6_out, not_7_out);
  or or_120 (or_120_out, BIN8[7], BIN8[5], not_5_out, BIN8[2], not_7_out);
  or or_121 (or_121_out, not_2_out, BIN8[5], not_5_out, not_6_out, BIN8[1]);
  or or_122 (or_122_out, BIN8[7], BIN8[5], not_4_out, not_6_out, not_7_out);
  or or_123 (or_123_out, BIN8[7], BIN8[4], BIN8[3], BIN8[2], BIN8[1]);
  or or_124 (or_124_out, BIN8[7], not_3_out, BIN8[4], BIN8[3], BIN8[1]);
  or or_125 (or_125_out, BIN8[7], not_2_out, BIN8[4], BIN8[3], not_6_out, not_7_out);
  or or_126 (or_126_out, BIN8[7], not_3_out, BIN8[4], BIN8[2], BIN8[1]);
  or or_127 (or_127_out, BIN8[7], BIN8[4], not_5_out, BIN8[2], not_7_out);
  or or_128 (or_128_out, BIN8[7], not_2_out, not_3_out, BIN8[4], not_6_out, not_7_out);
  or or_129 (or_129_out, BIN8[7], not_2_out, BIN8[3], BIN8[2], BIN8[1]);
  or or_130 (or_130_out, BIN8[7], not_3_out, not_4_out, BIN8[3], BIN8[2], not_7_out);
  or or_131 (or_131_out, BIN8[7], not_4_out, BIN8[3], not_6_out, BIN8[1]);
  or or_132 (or_132_out, BIN8[7], not_3_out, not_5_out, BIN8[2], BIN8[1]);
  or or_133 (or_133_out, BIN8[7], not_2_out, not_5_out, BIN8[2], not_7_out);
  or or_134 (or_134_out, BIN8[7], not_3_out, not_4_out, not_6_out, BIN8[1]);
  or or_135 (or_135_out, BIN8[7], not_4_out, not_5_out, not_6_out, not_7_out);
  or or_136 (or_136_out, BIN8[6], BIN8[5], BIN8[4], BIN8[3], not_8_out);
  or or_137 (or_137_out, BIN8[6], BIN8[5], BIN8[4], BIN8[3], not_7_out);
  or or_138 (or_138_out, BIN8[6], BIN8[5], BIN8[4], not_7_out, not_8_out);
  or or_139 (or_139_out, not_1_out, BIN8[6], BIN8[5], BIN8[3], not_7_out, BIN8[0]);
  or or_140 (or_140_out, BIN8[6], BIN8[5], BIN8[3], BIN8[1], not_8_out);
  or or_141 (or_141_out, BIN8[6], BIN8[5], BIN8[3], not_6_out, not_8_out);
  or or_142 (or_142_out, not_1_out, BIN8[6], BIN8[5], not_4_out, BIN8[2], BIN8[0]);
  or or_143 (or_143_out, BIN8[6], BIN8[5], not_4_out, not_5_out, BIN8[2]);
  or or_144 (or_144_out, BIN8[6], BIN8[5], not_6_out, not_7_out, not_8_out);
  or or_145 (or_145_out, BIN8[6], not_3_out, BIN8[4], BIN8[3], BIN8[2]);
  or or_146 (or_146_out, BIN8[6], not_3_out, BIN8[4], BIN8[3], BIN8[1]);
  or or_147 (or_147_out, not_1_out, BIN8[6], BIN8[4], BIN8[3], not_7_out, BIN8[0]);
  or or_148 (or_148_out, BIN8[6], not_3_out, BIN8[4], BIN8[2], not_8_out);
  or or_149 (or_149_out, BIN8[6], not_3_out, BIN8[4], BIN8[2], not_7_out);
  or or_150 (or_150_out, BIN8[6], BIN8[4], not_6_out, BIN8[1]);
  or or_151 (or_151_out, not_1_out, BIN8[6], not_3_out, BIN8[4], not_7_out, BIN8[0]);
  or or_152 (or_152_out, BIN8[6], BIN8[4], not_5_out, not_7_out, not_8_out);
  or or_153 (or_153_out, not_1_out, BIN8[6], not_3_out, BIN8[3], BIN8[1], BIN8[0]);
  or or_154 (or_154_out, BIN8[6], not_3_out, BIN8[3], BIN8[2], not_7_out, not_8_out);
  or or_155 (or_155_out, BIN8[6], BIN8[3], not_6_out, BIN8[1], not_8_out);
  or or_156 (or_156_out, not_1_out, BIN8[6], BIN8[3], not_6_out, not_7_out, BIN8[0]);
  or or_157 (or_157_out, BIN8[6], not_3_out, not_4_out, BIN8[3], not_7_out, not_8_out);
  or or_158 (or_158_out, not_1_out, BIN8[6], not_4_out, BIN8[2], BIN8[1], BIN8[0]);
  or or_159 (or_159_out, BIN8[6], not_4_out, not_5_out, BIN8[2], BIN8[1]);
  or or_160 (or_160_out, not_1_out, BIN8[6], not_4_out, not_5_out, BIN8[2], BIN8[0]);
  or or_161 (or_161_out, BIN8[6], not_3_out, not_6_out, BIN8[1], not_8_out);
  or or_162 (or_162_out, not_1_out, BIN8[6], not_3_out, not_6_out, not_7_out, BIN8[0]);
  or or_163 (or_163_out, BIN8[6], not_3_out, not_5_out, not_6_out, not_7_out);
  or or_164 (or_164_out, not_1_out, BIN8[5], BIN8[4], not_6_out, BIN8[1], BIN8[0]);
  or or_165 (or_165_out, BIN8[5], BIN8[4], BIN8[3], not_7_out, not_8_out);
  or or_166 (or_166_out, not_1_out, BIN8[5], BIN8[4], not_5_out, not_6_out, BIN8[0]);
  or or_167 (or_167_out, BIN8[5], BIN8[3], BIN8[2], BIN8[1], not_8_out);
  or or_168 (or_168_out, not_1_out, BIN8[5], BIN8[3], BIN8[2], not_7_out, BIN8[0]);
  or or_169 (or_169_out, not_2_out, BIN8[5], BIN8[3], BIN8[2], not_8_out);
  or or_170 (or_170_out, not_1_out, not_2_out, BIN8[5], not_6_out, BIN8[1], BIN8[0]);
  or or_171 (or_171_out, BIN8[5], not_4_out, BIN8[3], BIN8[1], not_8_out);
  or or_172 (or_172_out, not_1_out, BIN8[5], not_4_out, BIN8[3], not_7_out, BIN8[0]);
  or or_173 (or_173_out, BIN8[5], BIN8[3], not_6_out, not_7_out, not_8_out);
  or or_174 (or_174_out, BIN8[5], not_5_out, BIN8[2], not_7_out, not_8_out);
  or or_175 (or_175_out, not_1_out, not_2_out, BIN8[5], not_5_out, not_6_out, BIN8[0]);
  or or_176 (or_176_out, not_2_out, BIN8[5], not_4_out, not_7_out, not_8_out);
  or or_177 (or_177_out, not_3_out, BIN8[4], BIN8[3], BIN8[2], BIN8[1]);
  or or_178 (or_178_out, not_1_out, not_3_out, BIN8[4], BIN8[3], BIN8[2], BIN8[0]);
  or or_179 (or_179_out, not_3_out, BIN8[4], BIN8[3], BIN8[1], not_8_out);
  or or_180 (or_180_out, not_1_out, not_3_out, BIN8[4], BIN8[3], not_7_out, BIN8[0]);
  or or_181 (or_181_out, not_2_out, BIN8[4], BIN8[3], not_6_out, not_7_out, not_8_out);
  or or_182 (or_182_out, not_2_out, BIN8[4], BIN8[2], BIN8[1]);
  or or_183 (or_183_out, not_1_out, not_3_out, BIN8[4], BIN8[2], not_7_out, BIN8[0]);
  or or_184 (or_184_out, BIN8[4], not_5_out, BIN8[2], not_7_out, not_8_out);
  or or_185 (or_185_out, not_1_out, BIN8[4], not_5_out, not_6_out, BIN8[1], BIN8[0]);
  or or_186 (or_186_out, not_2_out, not_3_out, BIN8[4], not_6_out, not_7_out, not_8_out);
  or or_187 (or_187_out, not_1_out, not_3_out, BIN8[3], BIN8[2], BIN8[1], BIN8[0]);
  or or_188 (or_188_out, not_2_out, BIN8[3], BIN8[2], BIN8[1], not_8_out);
  or or_189 (or_189_out, not_1_out, not_2_out, BIN8[3], BIN8[2], not_7_out, BIN8[0]);
  or or_190 (or_190_out, not_3_out, not_4_out, BIN8[3], BIN8[2], not_7_out, not_8_out);
  or or_191 (or_191_out, not_1_out, not_3_out, not_4_out, BIN8[3], BIN8[1], BIN8[0]);
  or or_192 (or_192_out, not_4_out, BIN8[3], not_6_out, BIN8[1], not_8_out);
  or or_193 (or_193_out, not_1_out, not_4_out, BIN8[3], not_6_out, not_7_out, BIN8[0]);
  or or_194 (or_194_out, not_3_out, not_5_out, BIN8[2], BIN8[1], not_8_out);
  or or_195 (or_195_out, not_1_out, not_3_out, not_5_out, BIN8[2], not_7_out, BIN8[0]);
  or or_196 (or_196_out, not_2_out, not_5_out, BIN8[2], not_7_out, not_8_out);
  or or_197 (or_197_out, not_1_out, not_2_out, not_5_out, not_6_out, BIN8[1], BIN8[0]);
  or or_198 (or_198_out, not_3_out, not_4_out, not_6_out, BIN8[1], not_8_out);
  or or_199 (or_199_out, not_1_out, not_3_out, not_4_out, not_6_out, not_7_out, BIN8[0]);
  or or_200 (or_200_out, not_2_out, not_4_out, not_5_out, not_7_out, not_8_out);
  or or_201 (or_201_out, BIN8[7], BIN8[6], BIN8[5], BIN8[4], BIN8[2]);
  or or_202 (or_202_out, BIN8[7], BIN8[6], BIN8[5], BIN8[4], not_5_out, BIN8[1]);
  or or_203 (or_203_out, BIN8[7], BIN8[6], BIN8[5], BIN8[3], BIN8[2], not_7_out);
  or or_204 (or_204_out, BIN8[7], BIN8[6], BIN8[5], not_4_out, not_6_out);
  or or_205 (or_205_out, BIN8[7], BIN8[6], BIN8[4], BIN8[2], BIN8[1]);
  or or_206 (or_206_out, BIN8[7], not_3_out, BIN8[4], BIN8[3], not_6_out, not_7_out);
  or or_207 (or_207_out, BIN8[7], BIN8[6], BIN8[4], not_5_out, BIN8[2]);
  or or_208 (or_208_out, BIN8[7], BIN8[6], not_3_out, BIN8[3], BIN8[2], BIN8[1]);
  or or_209 (or_209_out, BIN8[7], BIN8[6], not_4_out, BIN8[3], BIN8[2], not_7_out);
  or or_210 (or_210_out, BIN8[7], BIN8[6], not_3_out, not_4_out, BIN8[3], BIN8[1]);
  or or_211 (or_211_out, BIN8[7], BIN8[6], not_3_out, not_5_out, BIN8[2], not_7_out);
  or or_212 (or_212_out, BIN8[7], BIN8[6], not_4_out, not_6_out, BIN8[1]);
  or or_213 (or_213_out, BIN8[7], BIN8[6], not_3_out, not_4_out, not_5_out, not_7_out);
  or or_214 (or_214_out, BIN8[7], not_2_out, BIN8[4], BIN8[3], not_6_out);
  or or_215 (or_215_out, BIN8[7], BIN8[5], BIN8[4], not_5_out, BIN8[2], BIN8[1]);
  or or_216 (or_216_out, BIN8[7], not_2_out, BIN8[4], not_6_out, not_7_out);
  or or_217 (or_217_out, BIN8[7], not_2_out, BIN8[5], not_4_out, BIN8[2]);
  or or_218 (or_218_out, BIN8[7], BIN8[5], not_4_out, not_5_out, not_6_out, BIN8[1]);
  or or_219 (or_219_out, BIN8[7], not_2_out, not_3_out, BIN8[4], BIN8[3], not_7_out);
  or or_220 (or_220_out, BIN8[7], not_2_out, not_3_out, BIN8[4], not_6_out);
  or or_221 (or_221_out, BIN8[7], not_3_out, not_4_out, BIN8[3], BIN8[2], BIN8[1]);
  or or_222 (or_222_out, BIN8[7], not_2_out, not_3_out, BIN8[3], not_6_out, not_7_out);
  or or_223 (or_223_out, BIN8[7], not_2_out, not_4_out, BIN8[2], BIN8[1]);
  or or_224 (or_224_out, BIN8[7], not_3_out, not_4_out, not_5_out, BIN8[2], not_7_out);
  or or_225 (or_225_out, BIN8[6], BIN8[5], BIN8[4], BIN8[2], BIN8[1], BIN8[0]);
  or or_226 (or_226_out, not_1_out, BIN8[6], BIN8[4], BIN8[3], not_6_out, not_8_out);
  or or_227 (or_227_out, not_1_out, BIN8[6], BIN8[4], BIN8[3], not_6_out, not_7_out);
  or or_228 (or_228_out, BIN8[6], BIN8[5], BIN8[4], not_5_out, BIN8[2], BIN8[1]);
  or or_229 (or_229_out, BIN8[6], BIN8[5], BIN8[4], not_5_out, BIN8[2], BIN8[0]);
  or or_230 (or_230_out, not_1_out, BIN8[6], BIN8[4], not_6_out, not_7_out, not_8_out);
  or or_231 (or_231_out, not_1_out, BIN8[6], BIN8[5], BIN8[3], BIN8[2], BIN8[1], BIN8[0]);
  or or_232 (or_232_out, not_1_out, BIN8[6], BIN8[5], not_4_out, BIN8[3], BIN8[2]);
  or or_233 (or_233_out, not_1_out, BIN8[6], BIN8[5], not_4_out, BIN8[3], BIN8[1], BIN8[0]);
  or or_234 (or_234_out, not_1_out, BIN8[6], BIN8[5], not_5_out, BIN8[2], BIN8[1], not_8_out);
  or or_235 (or_235_out, not_1_out, BIN8[6], BIN8[5], not_5_out, BIN8[2], not_7_out, BIN8[0]);
  or or_236 (or_236_out, not_1_out, BIN8[6], BIN8[5], not_4_out, BIN8[2], not_8_out);
  or or_237 (or_237_out, BIN8[6], BIN8[5], not_4_out, not_6_out, BIN8[1], BIN8[0]);
  or or_238 (or_238_out, not_1_out, BIN8[6], BIN8[5], not_4_out, not_5_out, BIN8[1], not_8_out);
  or or_239 (or_239_out, not_1_out, BIN8[6], BIN8[5], not_4_out, not_5_out, not_7_out, BIN8[0]);
  or or_240 (or_240_out, not_1_out, BIN8[6], not_3_out, BIN8[4], BIN8[3], not_7_out, not_8_out);
  or or_241 (or_241_out, not_1_out, BIN8[6], not_3_out, BIN8[4], BIN8[3], not_6_out);
  or or_242 (or_242_out, BIN8[6], BIN8[4], not_5_out, BIN8[2], BIN8[1], BIN8[0]);
  or or_243 (or_243_out, not_1_out, BIN8[6], not_3_out, BIN8[4], not_6_out, not_8_out);
  or or_244 (or_244_out, not_1_out, BIN8[6], not_3_out, BIN8[4], not_6_out, not_7_out);
  or or_245 (or_245_out, not_1_out, BIN8[6], not_4_out, BIN8[3], BIN8[2], BIN8[1]);
  or or_246 (or_246_out, not_1_out, BIN8[6], not_4_out, BIN8[3], BIN8[2], BIN8[0]);
  or or_247 (or_247_out, not_1_out, BIN8[6], not_3_out, BIN8[3], not_6_out, not_7_out, not_8_out);
  or or_248 (or_248_out, not_1_out, BIN8[6], not_3_out, not_5_out, BIN8[2], BIN8[1], BIN8[0]);
  or or_249 (or_249_out, not_1_out, BIN8[6], not_4_out, BIN8[2], BIN8[1], not_8_out);
  or or_250 (or_250_out, not_1_out, BIN8[6], not_4_out, BIN8[2], not_7_out, BIN8[0]);
  or or_251 (or_251_out, not_1_out, BIN8[6], not_4_out, not_5_out, BIN8[2], not_8_out);
  or or_252 (or_252_out, not_1_out, BIN8[6], not_3_out, not_4_out, not_5_out, BIN8[1], BIN8[0]);
  or or_253 (or_253_out, not_1_out, not_2_out, BIN8[5], BIN8[4], BIN8[3], BIN8[1], not_8_out);
  or or_254 (or_254_out, not_1_out, not_2_out, BIN8[5], BIN8[4], BIN8[3], not_7_out, BIN8[0]);
  or or_255 (or_255_out, not_1_out, not_2_out, BIN8[4], BIN8[3], BIN8[2], not_8_out);
  or or_256 (or_256_out, not_2_out, BIN8[5], BIN8[4], BIN8[3], not_6_out, BIN8[1]);
  or or_257 (or_257_out, not_1_out, not_2_out, BIN8[5], BIN8[4], not_5_out, not_7_out, not_8_out);
  or or_258 (or_258_out, not_1_out, not_2_out, BIN8[5], BIN8[4], not_6_out, BIN8[1]);
  or or_259 (or_259_out, not_1_out, not_2_out, BIN8[5], BIN8[4], not_6_out, BIN8[0]);
  or or_260 (or_260_out, not_1_out, BIN8[5], not_4_out, BIN8[3], BIN8[2], BIN8[1], BIN8[0]);
  or or_261 (or_261_out, not_1_out, not_2_out, BIN8[5], BIN8[3], not_6_out, BIN8[1], not_8_out);
  or or_262 (or_262_out, not_1_out, not_2_out, BIN8[5], BIN8[3], not_6_out, not_7_out, BIN8[0]);
  or or_263 (or_263_out, not_1_out, not_2_out, not_4_out, BIN8[3], not_6_out, not_8_out);
  or or_264 (or_264_out, not_2_out, BIN8[5], not_4_out, BIN8[2], BIN8[1], BIN8[0]);
  or or_265 (or_265_out, not_1_out, BIN8[5], not_4_out, not_5_out, BIN8[2], BIN8[1], not_8_out);
  or or_266 (or_266_out, not_1_out, BIN8[5], not_4_out, not_5_out, BIN8[2], not_7_out, BIN8[0]);
  or or_267 (or_267_out, not_1_out, not_2_out, BIN8[5], not_5_out, not_6_out, not_7_out, not_8_out);
  or or_268 (or_268_out, not_1_out, not_2_out, not_3_out, BIN8[4], BIN8[3], BIN8[2]);
  or or_269 (or_269_out, not_1_out, not_2_out, not_3_out, BIN8[4], BIN8[3], BIN8[1], BIN8[0]);
  or or_270 (or_270_out, not_1_out, not_2_out, not_3_out, BIN8[4], BIN8[2], not_8_out);
  or or_271 (or_271_out, not_1_out, not_2_out, not_3_out, BIN8[4], BIN8[2], not_7_out);
  or or_272 (or_272_out, not_1_out, not_2_out, BIN8[4], not_6_out, BIN8[1], BIN8[0]);
  or or_273 (or_273_out, not_1_out, not_2_out, not_3_out, BIN8[4], not_5_out, BIN8[1], not_8_out);
  or or_274 (or_274_out, not_1_out, not_2_out, not_3_out, BIN8[4], not_5_out, not_7_out, BIN8[0]);
  or or_275 (or_275_out, not_1_out, not_2_out, not_3_out, BIN8[3], BIN8[2], not_7_out, not_8_out);
  or or_276 (or_276_out, not_1_out, not_2_out, not_3_out, BIN8[3], not_6_out, BIN8[1], BIN8[0]);
  or or_277 (or_277_out, not_1_out, not_2_out, not_4_out, BIN8[3], not_6_out, not_7_out);
  or or_278 (or_278_out, not_1_out, not_3_out, not_4_out, not_5_out, BIN8[2], BIN8[1], BIN8[0]);
  or or_279 (or_279_out, not_1_out, not_2_out, not_3_out, not_5_out, not_6_out, BIN8[1], not_8_out);
  or or_280 (or_280_out, not_1_out, not_2_out, not_3_out, not_5_out, not_6_out, not_7_out, BIN8[0]);
  or or_281 (or_281_out, not_1_out, not_2_out, not_3_out, not_4_out, not_6_out, not_8_out);
  or or_282 (or_282_out, BIN8[7], BIN8[6], BIN8[5], BIN8[4], BIN8[2], BIN8[1]);
  or or_283 (or_283_out, BIN8[7], BIN8[5], BIN8[4], BIN8[3], BIN8[1]);
  or or_284 (or_284_out, BIN8[7], BIN8[6], BIN8[5], BIN8[4], not_5_out, BIN8[2]);
  or or_285 (or_285_out, BIN8[7], BIN8[5], BIN8[4], not_5_out, not_7_out);
  or or_286 (or_286_out, BIN8[7], BIN8[6], not_4_out, BIN8[3], BIN8[2], not_7_out);
  or or_287 (or_287_out, BIN8[7], BIN8[6], BIN8[5], not_4_out, not_6_out, BIN8[1]);
  or or_288 (or_288_out, BIN8[7], BIN8[6], BIN8[5], not_5_out, BIN8[2], BIN8[1]);
  or or_289 (or_289_out, BIN8[7], BIN8[6], BIN8[5], not_4_out, not_5_out, not_6_out);
  or or_290 (or_290_out, BIN8[7], BIN8[6], not_3_out, BIN8[3], not_7_out);
  or or_291 (or_291_out, BIN8[7], BIN8[6], BIN8[4], not_5_out, BIN8[2], BIN8[1]);
  or or_292 (or_292_out, BIN8[7], not_3_out, BIN8[4], not_5_out, BIN8[1]);
  or or_293 (or_293_out, BIN8[7], BIN8[6], not_3_out, not_4_out, BIN8[3], BIN8[2]);
  or or_294 (or_294_out, BIN8[7], BIN8[6], not_3_out, not_4_out, BIN8[2], not_7_out);
  or or_295 (or_295_out, BIN8[7], BIN8[6], not_4_out, not_5_out, not_6_out, BIN8[1]);
  or or_296 (or_296_out, BIN8[7], not_2_out, BIN8[5], BIN8[4], BIN8[3], not_6_out);
  or or_297 (or_297_out, BIN8[7], not_2_out, BIN8[5], BIN8[3], BIN8[1]);
  or or_298 (or_298_out, BIN8[7], BIN8[5], not_4_out, not_5_out, BIN8[2], BIN8[1]);
  or or_299 (or_299_out, BIN8[7], not_2_out, BIN8[5], not_4_out, not_5_out, BIN8[2]);
  or or_300 (or_300_out, BIN8[7], BIN8[5], not_5_out, not_6_out, not_7_out);
  or or_301 (or_301_out, BIN8[7], not_3_out, BIN8[3], BIN8[2], not_7_out);
  or or_302 (or_302_out, BIN8[7], not_2_out, BIN8[4], BIN8[3], not_6_out, BIN8[1]);
  or or_303 (or_303_out, BIN8[7], not_2_out, BIN8[4], not_5_out, not_6_out, not_7_out);
  or or_304 (or_304_out, BIN8[7], not_3_out, not_4_out, BIN8[3], not_7_out);
  or or_305 (or_305_out, BIN8[7], not_2_out, not_4_out, not_5_out, BIN8[2], BIN8[1]);
  or or_306 (or_306_out, BIN8[7], not_3_out, not_5_out, not_6_out, BIN8[1]);
  or or_307 (or_307_out, BIN8[6], BIN8[5], BIN8[4], BIN8[2], BIN8[1], BIN8[0]);
  or or_308 (or_308_out, not_1_out, BIN8[6], BIN8[5], BIN8[3], not_7_out, not_8_out);
  or or_309 (or_309_out, BIN8[5], BIN8[4], BIN8[3], BIN8[1], BIN8[0]);
  or or_310 (or_310_out, BIN8[6], BIN8[5], BIN8[4], not_5_out, BIN8[2], BIN8[1]);
  or or_311 (or_311_out, BIN8[6], BIN8[5], BIN8[4], not_5_out, BIN8[2], BIN8[0]);
  or or_312 (or_312_out, not_1_out, BIN8[5], BIN8[4], not_5_out, BIN8[1], not_8_out);
  or or_313 (or_313_out, BIN8[5], BIN8[4], not_5_out, not_7_out, BIN8[0]);
  or or_314 (or_314_out, not_1_out, BIN8[6], BIN8[5], not_4_out, BIN8[3], BIN8[2], not_8_out);
  or or_315 (or_315_out, BIN8[6], BIN8[5], not_4_out, BIN8[3], BIN8[2], not_7_out);
  or or_316 (or_316_out, BIN8[6], BIN8[5], not_4_out, not_6_out, BIN8[1], BIN8[0]);
  or or_317 (or_317_out, BIN8[6], BIN8[5], not_5_out, BIN8[2], BIN8[1], BIN8[0]);
  or or_318 (or_318_out, not_1_out, BIN8[6], BIN8[5], not_4_out, BIN8[2], not_7_out, not_8_out);
  or or_319 (or_319_out, BIN8[6], BIN8[5], not_4_out, not_5_out, not_6_out, BIN8[1]);
  or or_320 (or_320_out, BIN8[6], BIN8[5], not_4_out, not_5_out, not_6_out, BIN8[0]);
  or or_321 (or_321_out, not_1_out, BIN8[6], not_3_out, BIN8[3], BIN8[1], not_8_out);
  or or_322 (or_322_out, BIN8[6], not_3_out, BIN8[3], not_7_out, BIN8[0]);
  or or_323 (or_323_out, not_1_out, BIN8[6], BIN8[4], BIN8[3], not_6_out, not_7_out, not_8_out);
  or or_324 (or_324_out, BIN8[6], BIN8[4], not_5_out, BIN8[2], BIN8[1], BIN8[0]);
  or or_325 (or_325_out, not_1_out, BIN8[6], not_3_out, not_5_out, not_7_out, not_8_out);
  or or_326 (or_326_out, not_3_out, BIN8[4], not_5_out, BIN8[1], BIN8[0]);
  or or_327 (or_327_out, BIN8[6], not_3_out, not_4_out, BIN8[3], BIN8[2], BIN8[1]);
  or or_328 (or_328_out, not_1_out, BIN8[6], not_3_out, not_4_out, BIN8[2], BIN8[1], not_8_out);
  or or_329 (or_329_out, BIN8[6], not_3_out, not_4_out, BIN8[2], not_7_out, BIN8[0]);
  or or_330 (or_330_out, BIN8[6], not_4_out, not_5_out, not_6_out, BIN8[1], BIN8[0]);
  or or_331 (or_331_out, not_1_out, BIN8[5], BIN8[3], BIN8[2], not_7_out, not_8_out);
  or or_332 (or_332_out, not_2_out, BIN8[5], BIN8[4], BIN8[3], not_6_out, BIN8[1]);
  or or_333 (or_333_out, not_2_out, BIN8[5], BIN8[4], BIN8[3], not_6_out, BIN8[0]);
  or or_334 (or_334_out, not_1_out, not_2_out, BIN8[5], BIN8[4], not_5_out, not_6_out, not_8_out);
  or or_335 (or_335_out, not_2_out, BIN8[5], BIN8[3], BIN8[1], BIN8[0]);
  or or_336 (or_336_out, not_1_out, BIN8[5], not_4_out, BIN8[3], not_7_out, not_8_out);
  or or_337 (or_337_out, BIN8[5], not_4_out, not_5_out, BIN8[2], BIN8[1], BIN8[0]);
  or or_338 (or_338_out, not_2_out, BIN8[5], not_4_out, not_5_out, BIN8[2], BIN8[1]);
  or or_339 (or_339_out, not_2_out, BIN8[5], not_4_out, not_5_out, BIN8[2], BIN8[0]);
  or or_340 (or_340_out, not_1_out, BIN8[5], not_5_out, not_6_out, BIN8[1], not_8_out);
  or or_341 (or_341_out, BIN8[5], not_5_out, not_6_out, not_7_out, BIN8[0]);
  or or_342 (or_342_out, not_1_out, not_2_out, not_3_out, BIN8[4], BIN8[3], BIN8[2], not_8_out);
  or or_343 (or_343_out, not_2_out, not_3_out, BIN8[4], BIN8[3], BIN8[2], not_7_out);
  or or_344 (or_344_out, not_2_out, BIN8[4], BIN8[3], not_6_out, BIN8[1], BIN8[0]);
  or or_345 (or_345_out, not_1_out, not_2_out, not_3_out, BIN8[4], BIN8[3], not_7_out, not_8_out);
  or or_346 (or_346_out, not_1_out, not_2_out, not_3_out, BIN8[4], BIN8[2], not_7_out, not_8_out);
  or or_347 (or_347_out, not_1_out, not_2_out, BIN8[4], not_5_out, not_6_out, BIN8[1], not_8_out);
  or or_348 (or_348_out, not_2_out, BIN8[4], not_5_out, not_6_out, not_7_out, BIN8[0]);
  or or_349 (or_349_out, not_1_out, not_3_out, BIN8[3], BIN8[2], BIN8[1], not_8_out);
  or or_350 (or_350_out, not_3_out, BIN8[3], BIN8[2], not_7_out, BIN8[0]);
  or or_351 (or_351_out, not_1_out, not_3_out, not_4_out, BIN8[3], BIN8[1], not_8_out);
  or or_352 (or_352_out, not_3_out, not_4_out, BIN8[3], not_7_out, BIN8[0]);
  or or_353 (or_353_out, not_1_out, not_2_out, not_3_out, BIN8[3], not_6_out, not_7_out, not_8_out);
  or or_354 (or_354_out, not_2_out, not_4_out, not_5_out, BIN8[2], BIN8[1], BIN8[0]);
  or or_355 (or_355_out, not_1_out, not_3_out, not_5_out, BIN8[2], not_7_out, not_8_out);
  or or_356 (or_356_out, not_3_out, not_5_out, not_6_out, BIN8[1], BIN8[0]);
  or or_357 (or_357_out, not_1_out, not_2_out, not_3_out, not_4_out, not_6_out, not_7_out, not_8_out);
  and and_1 (BCD2[0], or_1_out, or_2_out, or_3_out, or_4_out, or_5_out, or_6_out, or_7_out, or_8_out, or_9_out);
  and and_2 (BCD1[2], or_25_out, or_26_out, or_27_out, or_28_out, or_29_out, or_30_out, or_31_out, or_32_out, or_33_out);
  and and_3 (BCD1[3], or_10_out, or_11_out, or_12_out, or_13_out, or_14_out, or_15_out, or_16_out, or_17_out, or_18_out, or_19_out, or_20_out, or_21_out, or_22_out, or_23_out, or_24_out);
  and and_4 (BCD1[1], or_34_out, or_35_out, or_36_out, or_37_out, or_38_out, or_39_out, or_40_out, or_41_out, or_42_out, or_43_out, or_44_out, or_45_out, or_46_out, or_47_out, or_48_out, or_49_out, or_50_out, or_51_out, or_52_out, or_53_out);
  and and_5 (BCD1[0], or_54_out, or_55_out, or_56_out, or_57_out, or_58_out, or_59_out, or_60_out, or_61_out, or_62_out, or_63_out, or_64_out, or_65_out, or_66_out, or_67_out, or_68_out, or_69_out, or_70_out, or_71_out, or_72_out, or_73_out, or_74_out, or_75_out, or_76_out, or_77_out, or_78_out, or_79_out, or_80_out, or_81_out, or_82_out, or_83_out, or_84_out, or_85_out, or_86_out, or_87_out, or_88_out, or_89_out, or_90_out, or_91_out, or_92_out, or_93_out);
  and and_6 (and_6_out, or_201_out, or_202_out, or_203_out, or_204_out, or_205_out, or_206_out, or_207_out, or_208_out, or_209_out, or_210_out, or_211_out, or_212_out, or_213_out, or_214_out, or_215_out, or_216_out, or_217_out, or_218_out, or_219_out, or_220_out, or_221_out, or_222_out, or_223_out, or_224_out, or_225_out, or_226_out, or_227_out, or_228_out, or_229_out, or_230_out, or_231_out, or_232_out, or_233_out, or_234_out, or_235_out, or_236_out, or_237_out, or_238_out, or_239_out, or_240_out, or_241_out);
  and and_7 (and_7_out, or_242_out, or_243_out, or_244_out, or_245_out, or_246_out, or_247_out, or_248_out, or_249_out, or_250_out, or_251_out, or_252_out, or_253_out, or_254_out, or_255_out, or_256_out, or_257_out, or_258_out, or_259_out, or_260_out, or_261_out, or_262_out, or_263_out, or_264_out, or_265_out, or_266_out, or_267_out, or_268_out, or_269_out, or_270_out, or_271_out, or_272_out, or_273_out, or_274_out, or_275_out, or_276_out, or_277_out, or_278_out, or_279_out, or_280_out, or_281_out);
  and and_8 (and_8_out, or_282_out, or_283_out, or_284_out, or_285_out, or_286_out, or_287_out, or_288_out, or_289_out, or_290_out, or_291_out, or_292_out, or_293_out, or_294_out, or_295_out, or_296_out, or_297_out, or_298_out, or_299_out, or_300_out, or_301_out, or_302_out, or_303_out, or_304_out, or_305_out, or_306_out, or_307_out, or_308_out, or_309_out, or_310_out, or_311_out, or_312_out, or_313_out, or_314_out, or_315_out, or_316_out, or_317_out, or_318_out, or_319_out);
  and and_9 (and_9_out, or_320_out, or_321_out, or_322_out, or_323_out, or_324_out, or_325_out, or_326_out, or_327_out, or_328_out, or_329_out, or_330_out, or_331_out, or_332_out, or_333_out, or_334_out, or_335_out, or_336_out, or_337_out, or_338_out, or_339_out, or_340_out, or_341_out, or_342_out, or_343_out, or_344_out, or_345_out, or_346_out, or_347_out, or_348_out, or_349_out, or_350_out, or_351_out, or_352_out, or_353_out, or_354_out, or_355_out, or_356_out, or_357_out);
  and and_10 (and_10_out, or_94_out, or_95_out, or_96_out, or_97_out, or_98_out, or_99_out, or_100_out, or_101_out, or_102_out, or_103_out, or_104_out, or_105_out, or_106_out, or_107_out, or_108_out, or_109_out, or_110_out, or_111_out, or_112_out, or_113_out, or_114_out, or_115_out, or_116_out, or_117_out, or_118_out, or_119_out, or_120_out, or_121_out, or_122_out, or_123_out, or_124_out, or_125_out, or_126_out, or_127_out, or_128_out, or_129_out, or_130_out, or_131_out, or_132_out, or_133_out, or_134_out, or_135_out, or_136_out, or_137_out, or_138_out, or_139_out, or_140_out, or_141_out, or_142_out, or_143_out, or_144_out, or_145_out, or_146_out, or_147_out);
  and and_11 (and_11_out, or_148_out, or_149_out, or_150_out, or_151_out, or_152_out, or_153_out, or_154_out, or_155_out, or_156_out, or_157_out, or_158_out, or_159_out, or_160_out, or_161_out, or_162_out, or_163_out, or_164_out, or_165_out, or_166_out, or_167_out, or_168_out, or_169_out, or_170_out, or_171_out, or_172_out, or_173_out, or_174_out, or_175_out, or_176_out, or_177_out, or_178_out, or_179_out, or_180_out, or_181_out, or_182_out, or_183_out, or_184_out, or_185_out, or_186_out, or_187_out, or_188_out, or_189_out, or_190_out, or_191_out, or_192_out, or_193_out, or_194_out, or_195_out, or_196_out, or_197_out, or_198_out, or_199_out, or_200_out);
  and and_12 (BCD0[2], and_6_out, and_7_out);
  and and_13 (BCD0[1], and_8_out, and_9_out);
  and and_14 (BCD0[3], and_10_out, and_11_out);

  assign BCD0[0] = BIN8[0];
  assign BCD2[3:1] = 3'b000;
  assign sign = BIN8[7];
endmodule

module ControlCPU (
  input  [11:0] Opcode12b,
  input  Z,
  input  COut,
  output [1:0] RA1,
  output [1:0] WA0,
  output [1:0] RA0,
  output [3:0] OpcodeALU,
  output MOV,
  output ST,
  output LD,
  output [7:0] IM8b,
  output [12:0] ADDR13b,
  output BNZ,
  output BCS,
  output MVI,
  output RegEnbl
);

  wire and_1_out, clock_1_out, clock_2_out, CZ_out, decoder_1_out0, decoder_1_out1, decoder_1_out2,
       decoder_1_out3, decoder_1_out4, decoder_1_out5, decoder_1_out6, nor_1_out, not_1_out, not_2_out,
       not_3_out, or_1_out, or_2_out, xor_1_out;
  wire [1:0] Status_q;
  wire [12:0] adder_1_out, multiplexer_2_out;

  Clock clock_1 (.out(clock_1_out));
  Multiplexer #(.width(2)) multiplexer_1 (.in0(Opcode12b[5:4]), .in1(Opcode12b[1:0]), .out(RA0), .sel(or_2_out));
  not not_1 (not_1_out, Status_q[0]);
  Register #(.width(2)) Status (.D({COut, Z}), .en(CZ_out), .clk(clock_1_out), .Q(Status_q));  // open: clr
  xor xor_1 (xor_1_out, Opcode12b[10], Opcode12b[11]);
  or or_1 (or_1_out, not_1_out, Status_q[1]);
  Multiplexer #(.width(13)) multiplexer_2 (
    .in0(13'h1), .in1({{4{Opcode12b[9]}}, Opcode12b[8:0]}), .out(multiplexer_2_out), .sel(and_1_out));
  and and_1 (and_1_out, xor_1_out, or_1_out);
  Adder #(.width(13)) adder_1 (.a(ADDR13b), .b(multiplexer_2_out), .out(adder_1_out));  // open: cin, cout
  and and_2 (BNZ, Opcode12b[10], xor_1_out);
  and and_3 (BCS, Opcode12b[11], xor_1_out);
  and and_4 (MVI, Opcode12b[10], Opcode12b[11]);
  not not_2 (not_2_out, xor_1_out);
  not not_3 (not_3_out, ST);
  nor nor_1 (nor_1_out, Opcode12b[10], Opcode12b[11]);
  Register #(.width(13)) register_1 (.D(adder_1_out), .en(1'b1), .clk(clock_2_out), .Q(ADDR13b));  // open: clr
  Clock clock_2 (.out(clock_2_out));
  and and_5 (RegEnbl, not_2_out, not_3_out);
  Decoder #(.select(4)) decoder_1 (
    .out0(decoder_1_out0), .out1(decoder_1_out1), .out2(decoder_1_out2), .out3(decoder_1_out3),
    .out4(decoder_1_out4), .out5(decoder_1_out5), .out6(decoder_1_out6), .out8(MOV), .out12(ST), .out13(LD),
    .sel(Opcode12b[9:6]), .en(nor_1_out));  // open: out7, out9, out10, out11, out14, out15
  or or_2 (or_2_out, decoder_1_out5, decoder_1_out6);
  or CZ (CZ_out, decoder_1_out0, decoder_1_out1, decoder_1_out2, decoder_1_out3, decoder_1_out4, decoder_1_out5, decoder_1_out6);

  assign IM8b = Opcode12b[9:2];
  assign OpcodeALU = Opcode12b[9:6];
  assign RA1 = Opcode12b[3:2];
  assign WA0 = Opcode12b[1:0];
endmodule
