// Logisim project MISCSIM.circ as structural Verilog: 2 circuits, main circuit main
module main (
  input  in_1,
  input  in_2,
  input  in_3,
  input  in_4,
  input  in_5,
  input  in_6,
  input  in_7,
  input  in_8,
  input  in_9
);

  wire nand_1_out, nand_4_out, nor_1_out, nor_3_out, nor_4_out, not_1_out, undriven;

  not not_1 (not_1_out, in_1);
  nor nor_1 (nor_1_out, in_8, in_9);
  nand nand_1 (nand_1_out, in_8, in_9);
  // NOR_Gate nor_2 has open pins: in0=in_2, in1=in_3, out=open
  // NAND_Gate nand_2 has open pins: in0=in_2, in1=in_3, out=open
  nor nor_3 (nor_3_out, in_4, in_5);
  // NAND_Gate nand_3 has open pins: in0=in_4, in1=in_5, out=open
  nor nor_4 (nor_4_out, in_6, in_7);
  nand nand_4 (nand_4_out, in_6, in_7);
  // AND_Gate and_1 has open pins: in1=nand_4_out, out=open
  // AND_Gate and_2 is placed but not wired
  // AND_Gate and_3 is placed but not wired
  // AND_Gate and_4 is placed but not wired
  // AND_Gate and_5 has open pins: in0=undriven, in1=nor_3_out, out=open
  // NOT_Gate not_2 has open pins: in=nor_4_out, out=open
  // AND_Gate and_6 has open pins: in0=nor_1_out, in1=nand_1_out, out=open
  // AND_Gate and_7 has open pins: in0=not_1_out, in4=nand_1_out, out=open
  // AND_Gate and_8 has open pins: in2=nand_1_out, out=open
  // AND_Gate and_9 has open pins: in1=nand_1_out, out=open
  // AND_Gate and_10 has open pins: in0=nand_1_out, in1=nor_4_out, out=open
  // NOT_Gate not_3 has open pins: in=nor_1_out, out=open
endmodule

module FourBitCLA (
  input  cin,
  input  a0,
  input  b0,
  input  a1,
  input  b1,
  input  a2,
  input  b2,
  input  a3,
  input  b3,
  output s0,
  output s1,
  output s2,
  output s3,
  output cout
);

  wire and_3_out, and_4_out, and_5_out, and_6_out, and_7_out, and_8_out, and_9_out, and_10_out, and_11_out,
       and_12_out, nand_1_out, nand_2_out, nand_3_out, nand_4_out, nor_1_out, nor_2_out, nor_3_out,
       nor_4_out, nor_7_out, nor_8_out, not_1_out, not_3_out, not_4_out, not_5_out;

  not not_1 (not_1_out, cin);
  nor nor_1 (nor_1_out, a0, b0);
  nand nand_1 (nand_1_out, a0, b0);
  nor nor_2 (nor_2_out, a1, b1);
  nand nand_2 (nand_2_out, a1, b1);
  nor nor_3 (nor_3_out, a2, b2);
  nand nand_3 (nand_3_out, a2, b2);
  nor nor_4 (nor_4_out, a3, b3);
  nand nand_4 (nand_4_out, a3, b3);
  // AND_Gate and_1 is placed but not wired
  // AND_Gate and_2 has open pins: in0=nand_2_out, in1=nor_1_out, out=open
  // NOT_Gate not_2 has open pins: in=nor_2_out, out=open
  and and_3 (and_3_out, ~nor_3_out, nand_3_out);  // AND_Gate
  and and_4 (and_4_out, not_1_out, nand_1_out, nand_2_out, nand_3_out);
  and and_5 (and_5_out, nand_2_out, nand_3_out, nor_1_out);
  and and_6 (and_6_out, nand_3_out, nor_2_out);
  not not_3 (not_3_out, nor_3_out);
  and and_7 (and_7_out, ~nor_4_out, nand_4_out);  // AND_Gate
  and and_8 (and_8_out, not_1_out, nand_4_out);
  buf and_9 (and_9_out, nand_4_out);  // AND_Gate
  and and_10 (and_10_out, nor_1_out, nand_4_out, nor_2_out);
  and and_11 (and_11_out, nand_4_out, nor_3_out);
  not not_4 (not_4_out, nor_4_out);
  // NOT_Gate not_5 has open pins: in=open, out=not_5_out
  nor nor_5 (cout, and_8_out, and_9_out, and_10_out, and_11_out, not_4_out);
  // AND_Gate and_12 has open pins: out=and_12_out
  // NOR_Gate nor_6 is placed but not wired
  // NOR_Gate nor_7 has open pins: out=nor_7_out
  nor nor_8 (nor_8_out, and_4_out, and_5_out, and_6_out, not_3_out);
  xor xor_1 (s0, not_5_out, and_12_out);
  // XOR_Gate xor_2 has open pins: out=s1
  xor xor_3 (s2, nor_7_out, and_3_out);
  xor xor_4 (s3, nor_8_out, and_7_out);
endmodule
